# Fritzing sketch april_battery_100kNTC (saved by Fritzing 0.7.11b)
breadboards: 1

parts:
  Part1 = Electric Imp April
  R3 = Resistor [tolerance=±5% resistance=100k package=THT]
  R4 = Temperature Sensor (Thermistor) [package=THT]

nets:
  N1: Part1.5, R4.pin_1
  N2: Part1.6, R3.Pin_1, R4.pin_0
  N3: Part1.8, R3.Pin_0

custom parts:
  Electric Imp April: Electric Imp Breakout Board with onboard 3.3V regulated power supply
