# Fritzing sketch april_battery_10kNTC (saved by Fritzing 0.7.11b)
breadboards: 1

parts:
  R2 = Temperature Sensor (Thermistor) [package=THT]
  Part1 = Electric Imp April
  R3 = Resistor [tolerance=±5% resistance=10k package=THT]

nets:
  N1: R2.pin_0, Part1.6, R3.Pin_1
  N2: R2.pin_1, Part1.5
  N3: Part1.8, R3.Pin_0

notes:
  Thermistor B57861S0103F040 has a resistance of 10k at 25C; the voltage at Pin 1 approximately equals 3.3/2 = 1.65V at room temperature.

custom parts:
  Electric Imp April: Electric Imp Breakout Board with onboard 3.3V regulated power supply
