# Fritzing sketch april_potentiometer_analog_in (saved by Fritzing 0.7.11b)

parts:
  R1 = Rotary Potentiometer (Small) [maximum_resistance=100kΩ]
  Part1 = Electric Imp Breakout

nets:
  GND: R1.leg1, Part1.9
  N1: R1.wiper, Part1.5
  N2: R1.leg2, Part1.8

notes:
  5k

custom parts:
  Electric Imp Breakout: Electric Imp Breakout Board with onboard 3.3V regulated power supply
