# Fritzing sketch april_pushbutton_demo (saved by Fritzing 0.7.10b)
breadboards: 1

parts:
  Part1 = Electric Imp April
  S1 = Pushbutton [package=THT]
  R1 = Resistor [tolerance=±5% resistance=10k package=THT]

nets:
  N1: Part1.4, S1.leg0, R1.Pin_1
  N2: Part1.8, R1.Pin_0
  N3: Part1.9, S1.leg1

notes:
  This 10k pullup resistor holds pin 7 at 3.3V (logic level high, or "1") unless the pushbutton is pressed
  When the button is pressed, pin7 is shorted to ground (logic level low, or "0")
  Note that this doesn't short 3.3V to ground - all the current has to go through our pull-up resistor

custom parts:
  Electric Imp April: Electric Imp Breakout Board with onboard 3.3V regulated power supply
