# Fritzing sketch april_pwm_led (saved by Fritzing 0.7.11b)
breadboards: 1

parts:
  Part1 = Electric Imp April
  LED1 = LED - 5mm [color="Red (633nm)" package="5 mm [THT]"]
  R1 = Resistor [tolerance=±5% resistance=370 package=THT]

nets:
  N1: Part1.6, R1.Pin_1
  N2: Part1.8, LED1.anode
  N3: LED1.cathode, R1.Pin_0

custom parts:
  Electric Imp April: Electric Imp Breakout Board with onboard 3.3V regulated power supply
