# Fritzing sketch april_servo_control (saved by Fritzing 0.7.11b)

parts:
  Part1 = Electric Imp April
  VCC1 = 4 x AAA Battery Mount
  J1 = Basic Servo

nets:
  N1: Part1.1, J1.pulse
  N2: Part1.9, J1.gnd
  N3: Part1.10, J1.vcc
  N4: Part1.15, VCC1.+
  N5: Part1.16, VCC1.-

notes:
  Most generic servos need between 4.5V and 6V to operate - you can operate with 4 AAs.

custom parts:
  Electric Imp April: Electric Imp Breakout Board with onboard 3.3V regulated power supply
