# Fritzing sketch april_shift_register (saved by Fritzing 0.7.11b)
breadboards: 1

parts:
  Part1 = Electric Imp April
  Part3 = Shift Register Breakout - 74HC595
  Part4 = Shift Register Breakout - 74HC595

nets:
  N1: Part1.1, Part3./RESET, Part4./RESET
  N2: Part1.3, Part3.CLOCK, Part4.CLOCK
  N3: Part1.4, Part3.SERIAL_IN
  N4: Part1.5, Part3./OUTPUT_ENABLE, Part4./OUTPUT_ENABLE
  VCC: Part1.8, Part3.VCC, Part4.VCC
  GND: Part1.9, Part3.GND, Part4.GND
  N5: Part3.SERIAL_OUT, Part4.SERIAL_IN

custom parts:
  Electric Imp April: Electric Imp Breakout Board with onboard 3.3V regulated power supply
