# Fritzing sketch generic_pot_circuit_bb (saved by Fritzing 0.7.10b)
breadboards: 1

parts:
  R1 = Rotary Potentiometer (Small) [maximum_resistance=100kΩ]
  LED1 = LED - 5mm [color="Red (633nm)" package="5 mm [THT]"]
  R2 = Resistor [tolerance=±5% resistance=220 package=THT]
  IC1 = IC, DIP package, 16 pins [chip_label=IC]  # not connected
  VCC1 = Battery

nets:
  N1: R1.leg1, LED1.cathode, VCC1.-
  N2: R1.leg2, VCC1.+
  N3: LED1.anode, R2.Pin_0
