# Fritzing sketch potentiometer_demo (saved by Fritzing 0.7.10b)
breadboards: 1

parts:
  R1 = Rotary Potentiometer (Small) [maximum_resistance=100kΩ]
  LED1 = LED - 5mm [color="Red (633nm)" package="5 mm [THT]"]
  R2 = Resistor [tolerance=±5% resistance=370 package=THT]
  Part1 = Electric Imp Breakout
  VCC1 = 4 x AAA Battery Mount

nets:
  GND: R1.leg1, Part1.16, VCC1.-
  N1: R1.wiper, Part1.5
  N2: R1.leg2, R2.Pin_1, Part1.8
  N3: LED1.cathode, Part1.6
  N4: LED1.anode, R2.Pin_0
  N5: Part1.12, Part1.13
  N6: Part1.15, VCC1.+

notes:
  370
  5k

custom parts:
  Electric Imp Breakout: Electric Imp Breakout Board with onboard 3.3V regulated power supply
