# Fritzing sketch thermalPrinter (saved by Fritzing 0.7.11b)

parts:
  Part2 = Thermal Printer
  Power_plug1 = Power plug
  Part1 = Electric Imp April

nets:
  N1: Part2.GND#0, Part1.11
  N2: Part2.VH, Part1.10
  N3: Part2.GND#2, Part1.9
  N4: Part2.RXD, Part1.3, Part1.5
  N5: Part2.TXD, Part1.4, Part1.6
  N6: Power_plug1.GND, Part1.16
  N7: Power_plug1.VCC, Part1.15
  N8: Part1.12, Part1.13

notes:
  5V-9V, 2A DC Power Supply

custom parts:
  Electric Imp April: Electric Imp Breakout Board with onboard 3.3V regulated power supply
